# Fritzing sketch weather-clock (saved by Fritzing 0.9.3b)
breadboards: 1

parts:
  Raspberry_Pi_1 = Raspberry Pi 3 [part_number=RPI-3-V1.2]
  Part1 = Adafruit 16-Channel PWM + Servo HAT [part_number="Adafruit #2327"]
  J1 = Basic Servo
  hc-sr1 = hc-sr04
  R1 = Resistor [tolerance=±5% resistance=220 package=THT]
  R2 = Resistor [tolerance=±5% resistance=470 package=THT]
  LED1 = LED - 5mm [color="Red (633nm)" package="5 mm [THT]"]
  LED2 = LED - 5mm [color="Red (633nm)" package="5 mm [THT]"]
  LED3 = LED - 5mm [color="Red (633nm)" package="5 mm [THT]"]
  R3 = Resistor [tolerance=±5% resistance=220 package=THT]
  R4 = Resistor [tolerance=±5% resistance=220 package=THT]
  R5 = Resistor [tolerance=±5% resistance=220 package=THT]

nets:
  N1: Raspberry_Pi_1.GIPO4, hc-sr1.Trig
  N2: Raspberry_Pi_1.GIPO17, R1.Pin_1, R2.Pin_0
  GND: Raspberry_Pi_1.GND, hc-sr1.GND, R2.Pin_1, R3.Pin_1, R4.Pin_1, R5.Pin_1
  N3: Raspberry_Pi_1.GIPO21, LED3.anode
  N4: Raspberry_Pi_1.GIPO20, LED2.anode
  N5: Raspberry_Pi_1.GIPO16, LED1.anode
  5V: Raspberry_Pi_1.5V, hc-sr1.VCC
  N6: Part1.#4, J1.pulse
  +5V: Part1.+5V, J1.vcc
  GND_2: Part1.GND, J1.gnd
  N7: hc-sr1.Echo, R1.Pin_0
  N8: LED1.cathode, R3.Pin_0
  N9: LED2.cathode, R4.Pin_0
  N10: LED3.cathode, R5.Pin_0

notes:
  Near
  Medium
  Far

custom parts:
  Adafruit 16-Channel PWM + Servo HAT: The Raspberry Pi is a wonderful little computer, but one thing it isn't very good at is controlling DC Servo Motors - these motors need very specific and repetitive timing pulses to set the position. Instead of asking the Pi Linux kernel to send these signals, pop on this handy HAT! It adds the capability to control 16 Servos with perfect timing. It can also do PWM up to 1.6 KHz with 12 bit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
